// Logisim project ALU.circ as structural Verilog: 3 circuits, main circuit main
module main (
  input  A,
  input  A_Invert,
  input  B,
  input  [1:0] Operation,
  input  B_Inver,
  input  Carry_in,
  output Result,
  output Carry_out
);

  wire adder_1_out, and_1_out, multiplexer_1_out, multiplexer_2_out, not_1_out, not_2_out, or_1_out,
       xor_1_out;

  not not_1 (not_1_out, A);
  not not_2 (not_2_out, B);
  Multiplexer #(.enable("false")) multiplexer_1 (.in0(A), .in1(not_1_out), .out(multiplexer_1_out), .sel(A_Invert));
  Multiplexer #(.enable("false")) multiplexer_2 (.in0(B), .in1(not_2_out), .out(multiplexer_2_out), .sel(B_Inver));
  and and_1 (and_1_out, multiplexer_1_out, multiplexer_2_out);
  or or_1 (or_1_out, multiplexer_1_out, multiplexer_2_out);
  xor xor_1 (xor_1_out, multiplexer_1_out, multiplexer_2_out);
  Adder #(.width(1)) adder_1 (
    .a(multiplexer_1_out), .b(multiplexer_2_out), .out(adder_1_out), .cin(Carry_in), .cout(Carry_out));
  Multiplexer #(.select(2), .enable("false")) multiplexer_3 (
    .in0(and_1_out), .in1(or_1_out), .in2(xor_1_out), .in3(adder_1_out), .out(Result), .sel(Operation));
endmodule

module ALU (
  input  [31:0] A,
  input  [31:0] B,
  input  [31:0] Old_Rd,
  input  [9:0] ALU_Opration,
  output [31:0] ALU_Result,
  output less_flag_unsign,
  output Overflow,
  output less_flag,
  output Zero_flag
);

  wire and_1_out, and_2_out, and_3_out, comparator_1_eq, comparator_1_gt, comparator_2_eq, comparator_2_gt,
       comparator_3_eq, comparator_3_gt, comparator_3_lt, main_1_carry_out, main_2_carry_out,
       main_3_carry_out, main_4_carry_out, main_5_carry_out, main_6_carry_out, main_7_carry_out,
       main_8_carry_out, main_9_carry_out, main_10_carry_out, main_11_carry_out, main_12_carry_out,
       main_13_carry_out, main_14_carry_out, main_15_carry_out, main_16_carry_out, main_17_carry_out,
       main_18_carry_out, main_19_carry_out, main_20_carry_out, main_21_carry_out, main_22_carry_out,
       main_23_carry_out, main_24_carry_out, main_25_carry_out, main_26_carry_out, main_27_carry_out,
       main_28_carry_out, main_29_carry_out, main_30_carry_out, main_31_carry_out, main_32_carry_out,
       not_2_out, not_3_out, not_4_out, not_5_out, not_6_out, not_7_out, or_1_out, Result_0, Result_1,
       Result_2, Result_3, Result_4, Result_5, Result_6, Result_7, Result_8, Result_9, Result_10, Result_11,
       Result_12, Result_13, Result_14, Result_15, Result_16, Result_17, Result_18, Result_19, Result_20,
       Result_21, Result_22, Result_23, Result_24, Result_25, Result_26, Result_27, Result_28, Result_29,
       Result_30, Result_31;
  wire [30:0] multiplier_1_out;
  wire [31:0] bit_extender_1_out, bit_extender_2_out, bit_extender_3_out, multiplexer_1_out, shifter_1_out,
       shifter_2_out, shifter_3_out, shifter_4_out;
  wire [31:31] xor_2_out;

  main main_1 (
    .A(A[0]), .B(B[0]), .Carry_in(ALU_Opration[0]), .A_Invert(ALU_Opration[1]), .B_Inver(ALU_Opration[2]),
    .Carry_out(main_1_carry_out), .Operation(ALU_Opration[4:3]), .Result(Result_0));
  main main_2 (
    .A(A[1]), .B(B[1]), .Carry_in(main_1_carry_out), .A_Invert(ALU_Opration[1]), .B_Inver(ALU_Opration[2]),
    .Carry_out(main_2_carry_out), .Operation(ALU_Opration[4:3]), .Result(Result_1));
  main main_3 (
    .A(A[2]), .B(B[2]), .Carry_in(main_2_carry_out), .A_Invert(ALU_Opration[1]), .B_Inver(ALU_Opration[2]),
    .Carry_out(main_3_carry_out), .Operation(ALU_Opration[4:3]), .Result(Result_2));
  main main_4 (
    .A(A[3]), .B(B[3]), .Carry_in(main_3_carry_out), .A_Invert(ALU_Opration[1]), .B_Inver(ALU_Opration[2]),
    .Carry_out(main_4_carry_out), .Operation(ALU_Opration[4:3]), .Result(Result_3));
  main main_5 (
    .A(A[4]), .B(B[4]), .Carry_in(main_4_carry_out), .A_Invert(ALU_Opration[1]), .B_Inver(ALU_Opration[2]),
    .Carry_out(main_5_carry_out), .Operation(ALU_Opration[4:3]), .Result(Result_4));
  main main_6 (
    .A(A[5]), .B(B[5]), .Carry_in(main_5_carry_out), .A_Invert(ALU_Opration[1]), .B_Inver(ALU_Opration[2]),
    .Carry_out(main_6_carry_out), .Operation(ALU_Opration[4:3]), .Result(Result_5));
  main main_7 (
    .A(A[6]), .B(B[6]), .Carry_in(main_6_carry_out), .A_Invert(ALU_Opration[1]), .B_Inver(ALU_Opration[2]),
    .Carry_out(main_7_carry_out), .Operation(ALU_Opration[4:3]), .Result(Result_6));
  main main_8 (
    .A(A[7]), .B(B[7]), .Carry_in(main_7_carry_out), .A_Invert(ALU_Opration[1]), .B_Inver(ALU_Opration[2]),
    .Carry_out(main_8_carry_out), .Operation(ALU_Opration[4:3]), .Result(Result_7));
  main main_9 (
    .A(A[8]), .B(B[8]), .Carry_in(main_8_carry_out), .A_Invert(ALU_Opration[1]), .B_Inver(ALU_Opration[2]),
    .Carry_out(main_9_carry_out), .Operation(ALU_Opration[4:3]), .Result(Result_8));
  main main_10 (
    .A(A[9]), .B(B[9]), .Carry_in(main_9_carry_out), .A_Invert(ALU_Opration[1]), .B_Inver(ALU_Opration[2]),
    .Carry_out(main_10_carry_out), .Operation(ALU_Opration[4:3]), .Result(Result_9));
  main main_11 (
    .A(A[10]), .B(B[10]), .Carry_in(main_10_carry_out), .A_Invert(ALU_Opration[1]),
    .B_Inver(ALU_Opration[2]), .Carry_out(main_11_carry_out), .Operation(ALU_Opration[4:3]),
    .Result(Result_10));
  main main_12 (
    .A(A[14]), .B(B[14]), .Carry_in(main_15_carry_out), .A_Invert(ALU_Opration[1]),
    .B_Inver(ALU_Opration[2]), .Carry_out(main_12_carry_out), .Operation(ALU_Opration[4:3]),
    .Result(Result_14));
  main main_13 (
    .A(A[11]), .B(B[11]), .Carry_in(main_11_carry_out), .A_Invert(ALU_Opration[1]),
    .B_Inver(ALU_Opration[2]), .Carry_out(main_13_carry_out), .Operation(ALU_Opration[4:3]),
    .Result(Result_11));
  main main_14 (
    .A(A[12]), .B(B[12]), .Carry_in(main_13_carry_out), .A_Invert(ALU_Opration[1]),
    .B_Inver(ALU_Opration[2]), .Carry_out(main_14_carry_out), .Operation(ALU_Opration[4:3]),
    .Result(Result_12));
  main main_15 (
    .A(A[13]), .B(B[13]), .Carry_in(main_14_carry_out), .A_Invert(ALU_Opration[1]),
    .B_Inver(ALU_Opration[2]), .Carry_out(main_15_carry_out), .Operation(ALU_Opration[4:3]),
    .Result(Result_13));
  main main_16 (
    .A(A[15]), .B(B[15]), .Carry_in(main_12_carry_out), .A_Invert(ALU_Opration[1]),
    .B_Inver(ALU_Opration[2]), .Carry_out(main_16_carry_out), .Operation(ALU_Opration[4:3]),
    .Result(Result_15));
  main main_17 (
    .A(A[16]), .B(B[16]), .Carry_in(main_16_carry_out), .A_Invert(ALU_Opration[1]),
    .B_Inver(ALU_Opration[2]), .Carry_out(main_17_carry_out), .Operation(ALU_Opration[4:3]),
    .Result(Result_16));
  main main_18 (
    .A(A[17]), .B(B[17]), .Carry_in(main_17_carry_out), .A_Invert(ALU_Opration[1]),
    .B_Inver(ALU_Opration[2]), .Carry_out(main_18_carry_out), .Operation(ALU_Opration[4:3]),
    .Result(Result_17));
  main main_19 (
    .A(A[18]), .B(B[18]), .Carry_in(main_18_carry_out), .A_Invert(ALU_Opration[1]),
    .B_Inver(ALU_Opration[2]), .Carry_out(main_19_carry_out), .Operation(ALU_Opration[4:3]),
    .Result(Result_18));
  main main_20 (
    .A(A[19]), .B(B[19]), .Carry_in(main_19_carry_out), .A_Invert(ALU_Opration[1]),
    .B_Inver(ALU_Opration[2]), .Carry_out(main_20_carry_out), .Operation(ALU_Opration[4:3]),
    .Result(Result_19));
  main main_21 (
    .A(A[20]), .B(B[20]), .Carry_in(main_20_carry_out), .A_Invert(ALU_Opration[1]),
    .B_Inver(ALU_Opration[2]), .Carry_out(main_21_carry_out), .Operation(ALU_Opration[4:3]),
    .Result(Result_20));
  main main_22 (
    .A(A[21]), .B(B[21]), .Carry_in(main_21_carry_out), .A_Invert(ALU_Opration[1]),
    .B_Inver(ALU_Opration[2]), .Carry_out(main_22_carry_out), .Operation(ALU_Opration[4:3]),
    .Result(Result_21));
  main main_23 (
    .A(A[22]), .B(B[22]), .Carry_in(main_22_carry_out), .A_Invert(ALU_Opration[1]),
    .B_Inver(ALU_Opration[2]), .Carry_out(main_23_carry_out), .Operation(ALU_Opration[4:3]),
    .Result(Result_22));
  main main_24 (
    .A(A[23]), .B(B[23]), .Carry_in(main_23_carry_out), .A_Invert(ALU_Opration[1]),
    .B_Inver(ALU_Opration[2]), .Carry_out(main_24_carry_out), .Operation(ALU_Opration[4:3]),
    .Result(Result_23));
  main main_25 (
    .A(A[24]), .B(B[24]), .Carry_in(main_24_carry_out), .A_Invert(ALU_Opration[1]),
    .B_Inver(ALU_Opration[2]), .Carry_out(main_25_carry_out), .Operation(ALU_Opration[4:3]),
    .Result(Result_24));
  main main_26 (
    .A(A[25]), .B(B[25]), .Carry_in(main_25_carry_out), .A_Invert(ALU_Opration[1]),
    .B_Inver(ALU_Opration[2]), .Carry_out(main_26_carry_out), .Operation(ALU_Opration[4:3]),
    .Result(Result_25));
  main main_27 (
    .A(A[26]), .B(B[26]), .Carry_in(main_26_carry_out), .A_Invert(ALU_Opration[1]),
    .B_Inver(ALU_Opration[2]), .Carry_out(main_27_carry_out), .Operation(ALU_Opration[4:3]),
    .Result(Result_26));
  main main_28 (
    .A(A[27]), .B(B[27]), .Carry_in(main_27_carry_out), .A_Invert(ALU_Opration[1]),
    .B_Inver(ALU_Opration[2]), .Carry_out(main_28_carry_out), .Operation(ALU_Opration[4:3]),
    .Result(Result_27));
  main main_29 (
    .A(A[28]), .B(B[28]), .Carry_in(main_28_carry_out), .A_Invert(ALU_Opration[1]),
    .B_Inver(ALU_Opration[2]), .Carry_out(main_29_carry_out), .Operation(ALU_Opration[4:3]),
    .Result(Result_28));
  main main_30 (
    .A(A[29]), .B(B[29]), .Carry_in(main_29_carry_out), .A_Invert(ALU_Opration[1]),
    .B_Inver(ALU_Opration[2]), .Carry_out(main_30_carry_out), .Operation(ALU_Opration[4:3]),
    .Result(Result_29));
  main main_31 (
    .A(A[30]), .B(B[30]), .Carry_in(main_30_carry_out), .A_Invert(ALU_Opration[1]),
    .B_Inver(ALU_Opration[2]), .Carry_out(main_31_carry_out), .Operation(ALU_Opration[4:3]),
    .Result(Result_30));
  main main_32 (
    .A(A[31]), .B(B[31]), .Carry_in(main_31_carry_out), .A_Invert(ALU_Opration[1]),
    .B_Inver(ALU_Opration[2]), .Carry_out(main_32_carry_out), .Operation(ALU_Opration[4:3]),
    .Result(Result_31));
  xor xor_1 (Overflow, main_31_carry_out, main_32_carry_out);
  // Probe on main_32_carry_out
  or or_1 (or_1_out, Result_0, Result_1, Result_2, Result_3, Result_4, Result_5, Result_6, Result_7, Result_8, Result_9, Result_10, Result_11, Result_12, Result_13, Result_14, Result_15, Result_16, Result_17, Result_18, Result_19, Result_20, Result_21, Result_22, Result_23, Result_24, Result_25, Result_26, Result_27, Result_28, Result_29, Result_30, Result_31);
  not not_1 (Zero_flag, or_1_out);
  Shifter #(.width(32)) shifter_1 (.in(A), .\dist (B[4:0]), .out(shifter_1_out));
  Shifter #(.width(32), .shift("lr")) shifter_2 (.in(A), .\dist (B[4:0]), .out(shifter_2_out));
  Shifter #(.width(32), .shift("ar")) shifter_3 (.in(A), .\dist (B[4:0]), .out(shifter_3_out));
  Shifter #(.width(32), .shift("rr")) shifter_4 (.in(A), .\dist (B[4:0]), .out(shifter_4_out));
  Comparator #(.width(32), .mode("unsigned")) comparator_1 (
    .a(A), .b(B), .gt(comparator_1_gt), .eq(comparator_1_eq), .lt(less_flag_unsign));
  Comparator #(.width(32)) comparator_2 (.a(A), .b(B), .gt(comparator_2_gt), .eq(comparator_2_eq), .lt(less_flag));
  Comparator #(.width(32)) comparator_3 (
    .a(A), .b(B), .gt(comparator_3_gt), .eq(comparator_3_eq), .lt(comparator_3_lt));
  Multiplexer #(.select(2), .width(32), .enable("false")) multiplexer_1 (
    .in0(shifter_1_out), .in1(shifter_2_out), .in2(shifter_3_out), .in3(shifter_4_out),
    .out(multiplexer_1_out), .sel(ALU_Opration[6:5]));
  not not_2 (not_2_out, comparator_1_eq);
  not not_3 (not_3_out, comparator_2_gt);
  not not_4 (not_4_out, comparator_2_eq);
  not not_5 (not_5_out, comparator_3_gt);
  not not_6 (not_6_out, comparator_3_lt);
  not not_7 (not_7_out, comparator_1_gt);
  Multiplier #(.width(31)) multiplier_1 (.a(A[30:0]), .b(B[30:0]), .out(multiplier_1_out));  // open: cin, cout
  and and_1 (and_1_out, not_7_out, not_2_out, less_flag_unsign);
  and and_2 (and_2_out, not_3_out, not_4_out, less_flag);
  and and_3 (and_3_out, not_5_out, comparator_3_eq, not_6_out);
  xor xor_2 (xor_2_out[31], A[31], B[31]);
  assign bit_extender_1_out = {{31{1'b0}}, and_1_out};  // Bit_Extender bit_extender_1
  assign bit_extender_2_out = {{31{and_2_out}}, and_2_out};  // Bit_Extender bit_extender_2
  assign bit_extender_3_out = {{31{and_3_out}}, and_3_out};  // Bit_Extender bit_extender_3
  Multiplexer #(.select(3), .width(32), .enable("false")) multiplexer_2 (
    .in0({Result_31, Result_30, Result_29, Result_28, Result_27, Result_26, Result_25, Result_24, Result_23, Result_22, Result_21, Result_20, Result_19, Result_18, Result_17, Result_16, Result_15, Result_14, Result_13, Result_12, Result_11, Result_10, Result_9, Result_8, Result_7, Result_6, Result_5, Result_4, Result_3, Result_2, Result_1, Result_0}),
    .in1(multiplexer_1_out), .in2(bit_extender_1_out), .in3(bit_extender_2_out), .in4(bit_extender_3_out),
    .in5({xor_2_out[31], multiplier_1_out}), .in6(B), .in7({Old_Rd[31:16], B[15:0]}), .out(ALU_Result),
    .sel(ALU_Opration[9:7]));

  // Other names for the same wires on the sheet: Least_Imm16[15:0] = B[15:0]; shift_amount_5bit_least[4:0] = B[4:0];
  //   carry_in = ALU_Opration[0]; A_Invert = ALU_Opration[1]; B_Invert = ALU_Opration[2];
  //   operation[1:0] = ALU_Opration[4:3]; shift_selector[1:0] = ALU_Opration[6:5];
  //   ALU_selector[2:0] = ALU_Opration[9:7]

  // Notes on the sheet:
  //   SLL
  //   SRL
  //   SRA
  //   ROR
  //   Unsigned
  //   Signed
  //   Equal
  //   SSET
  //   SET
endmodule

module ALU_CIR (
);

  ALU alu_1 ();  // open: ALU_Result, less_flag_unsign, Overflow, less_flag, Zero_flag, A, B, ALU_Opration, Old_Rd
endmodule
