// Logisim project Data_Mem.circ as structural Verilog: 2 circuits, main circuit main
module main (
  input  [31:0] Alu_Result,
  input  Mem_Write,
  input  Mem_Read,
  input  Clk,
  input  [31:0] Data_In,
  output [31:0] Data_Out
);

  RAM #(.addrWidth(20), .dataWidth(32), .trigger("falling"), .databus("bibus")) ram_1 (
    .addr(Alu_Result[19:0]), .we(Mem_Write), .oe(Mem_Read), .clk(Clk), .din(Data_In), .dout(Data_Out));
  // Probe on Data_Out
endmodule

module Data_Mem_block (
);

  main main_1 ();  // open: Mem_Write, Mem_Read, Clk, Data_In, Data_Out, Alu_Result
endmodule
