// Logisim project Detecting_raw_hazard.circ as structural Verilog: 1 circuit, main circuit main
module main (
  input  in_1,
  input  [4:0] in_2,
  input  in_3,
  input  [4:0] in_4,
  input  [4:0] in_5,
  input  in_6,
  input  [4:0] in_7,
  input  [4:0] in_8
);

  wire and_1_out, and_2_out, and_3_out, and_4_out, and_5_out, and_6_out, and_7_out, and_8_out, and_9_out,
       and_10_out, and_11_out, and_12_out, comparator_1_eq, comparator_1_gt, comparator_1_lt,
       comparator_2_eq, comparator_2_gt, comparator_2_lt, comparator_3_eq, comparator_3_gt, comparator_3_lt,
       comparator_4_eq, comparator_4_gt, comparator_4_lt, comparator_5_eq, comparator_5_gt, comparator_5_lt,
       comparator_6_eq, comparator_6_gt, comparator_6_lt, not_1_out, not_2_out, not_3_out, not_4_out,
       not_5_out, not_6_out, not_7_out, not_8_out, not_9_out, not_10_out, not_11_out, not_12_out, or_1_out,
       or_2_out, or_3_out, or_4_out, or_5_out, or_6_out;

  or or_1 (or_1_out, in_7[0], in_7[1], in_7[2], in_7[3], in_7[4]);
  Comparator #(.width(5)) comparator_1 (
    .a(in_7), .b(in_2), .gt(comparator_1_gt), .eq(comparator_1_eq), .lt(comparator_1_lt));
  or or_2 (or_2_out, in_7[0], in_7[1], in_7[2], in_7[3], in_7[4]);
  Comparator #(.width(5)) comparator_2 (
    .a(in_7), .b(in_4), .gt(comparator_2_gt), .eq(comparator_2_eq), .lt(comparator_2_lt));
  or or_3 (or_3_out, in_7[0], in_7[1], in_7[2], in_7[3], in_7[4]);
  Comparator #(.width(5)) comparator_3 (
    .a(in_7), .b(in_5), .gt(comparator_3_gt), .eq(comparator_3_eq), .lt(comparator_3_lt));
  not not_1 (not_1_out, comparator_1_gt);
  not not_2 (not_2_out, comparator_1_lt);
  not not_3 (not_3_out, comparator_2_gt);
  not not_4 (not_4_out, comparator_2_lt);
  not not_5 (not_5_out, comparator_3_gt);
  not not_6 (not_6_out, comparator_3_lt);
  and and_1 (and_1_out, not_1_out, comparator_1_eq, not_2_out);
  and and_2 (and_2_out, not_3_out, comparator_2_eq, not_4_out);
  and and_3 (and_3_out, not_5_out, comparator_3_eq, not_6_out);
  and and_4 (and_4_out, or_1_out, and_1_out, in_1);
  and and_5 (and_5_out, or_2_out, and_2_out, in_3);
  and and_6 (and_6_out, or_3_out, and_3_out, in_6);
  or or_4 (or_4_out, in_8[0], in_8[1], in_8[2], in_8[3], in_8[4]);
  Comparator #(.width(5)) comparator_4 (
    .a(in_8), .b(in_2), .gt(comparator_4_gt), .eq(comparator_4_eq), .lt(comparator_4_lt));
  or or_5 (or_5_out, in_8[0], in_8[1], in_8[2], in_8[3], in_8[4]);
  Comparator #(.width(5)) comparator_5 (
    .a(in_8), .b(in_4), .gt(comparator_5_gt), .eq(comparator_5_eq), .lt(comparator_5_lt));
  or or_6 (or_6_out, in_8[0], in_8[1], in_8[2], in_8[3], in_8[4]);
  Comparator #(.width(5)) comparator_6 (
    .a(in_8), .b(in_5), .gt(comparator_6_gt), .eq(comparator_6_eq), .lt(comparator_6_lt));
  not not_7 (not_7_out, comparator_4_gt);
  not not_8 (not_8_out, comparator_4_lt);
  not not_9 (not_9_out, comparator_5_gt);
  not not_10 (not_10_out, comparator_5_lt);
  not not_11 (not_11_out, comparator_6_gt);
  not not_12 (not_12_out, comparator_6_lt);
  and and_7 (and_7_out, not_7_out, comparator_4_eq, not_8_out);
  and and_8 (and_8_out, not_9_out, comparator_5_eq, not_10_out);
  and and_9 (and_9_out, not_11_out, comparator_6_eq, not_12_out);
  and and_10 (and_10_out, or_4_out, and_7_out, in_1);
  and and_11 (and_11_out, or_5_out, and_8_out, in_3);
  and and_12 (and_12_out, or_6_out, and_9_out, in_6);

  // Other names for the same wires on the sheet: EX_regWrite = in_1; MEM_regWrite = in_3; Rd_EX[4:0] = in_2;
  //   Rd_MEM[4:0] = in_4; Rd_WB[4:0] = in_5; RS[4:0] = in_7; Rt[4:0] = in_8; WB_regWrite = in_6

  // Notes on the sheet:
  //   ForwardA
  //   1
  //   2
  //   3
  //   ForwardB
  //   1
  //   2
  //   3
endmodule
