// Logisim project Forward.circ as structural Verilog: 2 circuits, main circuit main
// Reg_Wr_Ex
module main (
  input  Reg_Wr_EX,
  input  Reg_Wr_MEM,
  input  Reg_Wr_WB,
  input  [4:0] Rs,
  input  [4:0] Rt,
  input  [4:0] Rd_EX,
  input  [4:0] Rd_MEM,
  input  [4:0] Rd_WB,
  input  MEM_Read_EX,
  output [1:0] Forwad_A,
  output Stall,
  output [1:0] Forwad_B
);

  wire and_1_out, and_2_out, and_3_out, and_4_out, and_5_out, and_6_out, comparator_1_eq, comparator_2_eq,
       comparator_3_eq, comparator_4_eq, comparator_5_eq, comparator_6_eq, comparator_7_eq, comparator_8_eq,
       comparator_9_eq, comparator_10_eq, not_3_out, not_4_out, not_5_out, not_6_out, or_5_out,
       Rs_notequal_zero, Rt_notequal_zero;

  Comparator #(.width(5)) comparator_1 (.a(Rs), .b({5{1'b0}}), .eq(comparator_1_eq));  // open: gt, lt
  Comparator #(.width(5)) comparator_2 (.a(Rt), .b({5{1'b0}}), .eq(comparator_2_eq));  // open: gt, lt
  not not_1 (Rs_notequal_zero, comparator_1_eq);
  not not_2 (Rt_notequal_zero, comparator_2_eq);
  Comparator #(.width(5)) comparator_3 (.a(Rs), .b(Rd_EX), .eq(comparator_3_eq));  // open: gt, lt
  Comparator #(.width(5)) comparator_4 (.a(Rs), .b(Rd_MEM), .eq(comparator_4_eq));  // open: gt, lt
  Comparator #(.width(5)) comparator_5 (.a(Rs), .b(Rd_WB), .eq(comparator_5_eq));  // open: gt, lt
  Comparator #(.width(5)) comparator_6 (.a(Rt), .b(Rd_EX), .eq(comparator_6_eq));  // open: gt, lt
  Comparator #(.width(5)) comparator_7 (.a(Rt), .b(Rd_MEM), .eq(comparator_7_eq));  // open: gt, lt
  Comparator #(.width(5)) comparator_8 (.a(Rt), .b(Rd_WB), .eq(comparator_8_eq));  // open: gt, lt
  and and_1 (and_1_out, Rs_notequal_zero, comparator_3_eq, Reg_Wr_EX);
  not not_3 (not_3_out, and_1_out);
  and and_2 (and_2_out, Rt_notequal_zero, comparator_6_eq, Reg_Wr_EX);
  not not_4 (not_4_out, and_2_out);
  and and_3 (and_3_out, not_3_out, Rs_notequal_zero, comparator_4_eq, Reg_Wr_MEM);
  not not_5 (not_5_out, and_3_out);
  and and_4 (and_4_out, not_4_out, Rt_notequal_zero, comparator_7_eq, Reg_Wr_MEM);
  not not_6 (not_6_out, and_4_out);
  and and_5 (and_5_out, not_3_out, not_5_out, Rs_notequal_zero, comparator_5_eq, Reg_Wr_WB);
  and and_6 (and_6_out, not_4_out, not_6_out, Rt_notequal_zero, comparator_8_eq, Reg_Wr_WB);
  or or_1 (Forwad_A[0], and_1_out, and_5_out);
  or or_2 (Forwad_A[1], and_3_out, and_5_out);
  or or_3 (Forwad_B[0], and_2_out, and_6_out);
  or or_4 (Forwad_B[1], and_4_out, and_6_out);
  Comparator #(.width(2)) comparator_9 (.a(Forwad_A), .b(2'b01), .eq(comparator_9_eq));  // open: gt, lt
  Comparator #(.width(2)) comparator_10 (.a(2'b01), .b(Forwad_B), .eq(comparator_10_eq));  // open: gt, lt
  or or_5 (or_5_out, comparator_9_eq, comparator_10_eq);
  and and_7 (Stall, MEM_Read_EX, Rt_notequal_zero, Rs_notequal_zero, or_5_out);

  // Notes on the sheet:
  //   from_ALU_Stage (01)
  //   from_ALU_Stage (01)
  //   from_MEM_Stage (10)
  //   Forward_A
  //   from_MEM_Stage (10)
  //   from_WB_Stage(11)
  //   Forward_B
  //   from_WB_Stage(11)
endmodule

module BLOCK (
);

  main main_1 ();  // open: Reg_Wr_EX, Reg_Wr_MEM, Reg_Wr_WB, Rs, Rt, Forwad_A, Rd_EX, Rd_MEM, Rd_WB, Stall, MEM_Read_EX, Forwad_B
endmodule
