// Logisim project Instruction_Mem.circ as structural Verilog: 2 circuits, main circuit main
module main (
  input  [19:0] Address,
  output [31:0] Instruction
);

  ROM #(.addrWidth(20), .dataWidth(32)) rom_1 (.addr(Address), .data(Instruction));
endmodule

module Instruction_mem_block (
);

  main main_1 ();  // open: Address, Instruction
endmodule
