// Logisim project PC_Control_Unit.circ as structural Verilog: 2 circuits, main circuit main
module main (
  input  in_1,
  input  in_2,
  input  in_3,
  input  [4:0] op_code_5bit,
  output Kill_1,
  output [1:0] out_6,
  output Kill_2
);

  wire and_1_out, and_2_out, and_3_out, and_4_out, and_5_out, and_6_out, decoder_1_out15, decoder_1_out18,
       decoder_1_out19, decoder_1_out20, decoder_1_out21, decoder_1_out22, decoder_1_out23, not_1_out,
       not_2_out, not_3_out, not_4_out;

  Decoder #(.select(5)) decoder_1 (
    .out15(decoder_1_out15), .out18(decoder_1_out18), .out19(decoder_1_out19), .out20(decoder_1_out20),
    .out21(decoder_1_out21), .out22(decoder_1_out22), .out23(decoder_1_out23), .sel(op_code_5bit));  // open: out0, out1, out2, out3, out4, out5, out6, out7, out8, out9, out10, out11, out12, out13, out14, out16, out17, out24, out25, out26, out27, out28, out29, out30, out31, en
  and and_1 (and_1_out, decoder_1_out18, in_1);
  not not_1 (not_1_out, in_1);
  and and_2 (and_2_out, not_1_out, decoder_1_out19);
  and and_3 (and_3_out, decoder_1_out20, in_2);
  not not_2 (not_2_out, in_2);
  and and_4 (and_4_out, not_2_out, decoder_1_out21);
  and and_5 (and_5_out, decoder_1_out22, in_3);
  not not_3 (not_3_out, in_3);
  and and_6 (and_6_out, not_3_out, decoder_1_out23);
  not not_4 (not_4_out, Kill_2);
  or or_1 (Kill_2, and_1_out, and_2_out, and_3_out, and_4_out, and_5_out, and_6_out);
  and and_7 (out_6[0], decoder_1_out15, not_4_out);
  or or_2 (Kill_1, out_6[0], Kill_2);

  assign out_6[1] = Kill_2;

  // Other names for the same wires on the sheet: less_flag = in_2; less_unsing_flag = in_3; zero_fLAG = in_1

  // Notes on the sheet:
  //   jump
  //   BEQ
  //   BEQ
  //   BNQ
  //   BLT
  //   BGE
  //   BLTU
  //   BGEU
endmodule

module PC_Unit_Control (
);

  main main_1 ();  // open: in_1, in_2, in_3, op_code_5bit, out_6, Kill_1, Kill_2
endmodule
