// Logisim project alu_cont_unit.circ as structural Verilog: 2 circuits, main circuit main
module main (
);

  block1 block1_1 ();  // open: op_code, ALU_OP, func
endmodule

module block1 (
  input  [5:0] op_code,
  input  [3:0] func,
  output [9:0] ALU_OP
);

  wire and_2_out, and_3_out, and_4_out, and_5_out, and_6_out, and_7_out, and_8_out, and_9_out, and_10_out,
       and_11_out, and_13_out, and_14_out, and_16_out, and_17_out, and_18_out, and_19_out, and_20_out,
       and_21_out, and_22_out, not_1_out, not_2_out, not_3_out, not_4_out, not_5_out, not_7_out, not_8_out,
       not_9_out, not_10_out, or_1_out;
  wire [3:2] controlled_buffer_1_out;
  wire [9:1] and_12_out, and_23_out;

  or or_1 (or_1_out, op_code[5], op_code[4], op_code[3], op_code[2], op_code[1], op_code[0]);
  not not_1 (not_1_out, or_1_out);
  assign {controlled_buffer_1_out, and_23_out[6:5]} = not_1_out ? func : 4'bz;  // Controlled_Buffer controlled_buffer_1
  not not_2 (not_2_out, op_code[4]);
  not not_3 (not_3_out, op_code[3]);
  not not_4 (not_4_out, op_code[2]);
  not not_5 (not_5_out, op_code[1]);
  not not_6 (and_12_out[5], op_code[0]);
  not not_7 (not_7_out, controlled_buffer_1_out[3]);
  not not_8 (not_8_out, controlled_buffer_1_out[2]);
  not not_9 (not_9_out, and_23_out[6]);
  not not_10 (not_10_out, and_23_out[5]);
  and and_1 (and_12_out[9], not_2_out, not_4_out, not_5_out, and_12_out[5]);
  and and_2 (and_2_out, op_code[4], op_code[2]);
  and and_3 (and_3_out, op_code[2], op_code[1]);
  and and_4 (and_4_out, not_2_out, not_3_out, not_4_out);
  and and_5 (and_5_out, op_code[4], op_code[2], not_5_out);
  and and_6 (and_6_out, not_2_out, not_3_out, and_12_out[5]);
  and and_7 (and_7_out, op_code[1], op_code[0]);
  and and_8 (and_8_out, not_4_out, not_5_out);
  and and_9 (and_9_out, not_4_out, and_12_out[5]);
  and and_10 (and_10_out, op_code[2], and_12_out[5]);
  and and_11 (and_11_out, op_code[4], op_code[1]);
  and and_12 (and_12_out[1], op_code[2], and_12_out[5]);
  or or_2 (and_12_out[8], and_2_out, and_3_out);
  or or_3 (and_12_out[7], and_4_out, and_5_out, and_6_out);
  or or_4 (and_12_out[6], and_7_out, op_code[2]);
  or or_5 (and_12_out[4], not_3_out, and_8_out);
  or or_6 (and_12_out[3], not_3_out, and_9_out);
  or or_7 (and_12_out[2], and_10_out, and_11_out);
  and and_13 (and_13_out, controlled_buffer_1_out[3], not_8_out, not_9_out, not_10_out);
  or or_8 (and_23_out[9], and_13_out, and_14_out);
  and and_14 (and_14_out, controlled_buffer_1_out[3], controlled_buffer_1_out[2], and_23_out[5]);
  and and_15 (and_23_out[8], controlled_buffer_1_out[2], and_23_out[6]);
  and and_16 (and_16_out, not_7_out, not_8_out);
  or or_9 (and_23_out[7], and_16_out, and_17_out, and_18_out);
  and and_17 (and_17_out, controlled_buffer_1_out[3], controlled_buffer_1_out[2], and_23_out[5]);
  and and_18 (and_18_out, not_7_out, and_23_out[6], not_10_out);
  or or_10 (and_23_out[4], not_7_out, and_19_out);
  and and_19 (and_19_out, not_8_out, not_9_out);
  or or_11 (and_23_out[3], not_7_out, and_20_out);
  and and_20 (and_20_out, not_8_out, not_10_out);
  and and_21 (and_21_out, not_7_out, and_23_out[5]);
  or or_12 (and_23_out[2], and_21_out, and_22_out);
  and and_22 (and_22_out, controlled_buffer_1_out[3], controlled_buffer_1_out[2]);
  and and_23 (and_23_out[1], controlled_buffer_1_out[3], controlled_buffer_1_out[2]);
  Multiplexer #(.width(10)) multiplexer_1 (
    .in0({and_12_out, op_code[1]}), .in1({and_23_out, and_23_out[5]}), .out(ALU_OP), .sel(not_1_out));  // open: en
endmodule
