// Logisim project alu_control_unit.circ as structural Verilog: 2 circuits, main circuit OP_CODE
module main (
);

  OP_CODE op_code_1 ();  // open: opcode, ALU_OP, func_4bit
endmodule

module OP_CODE (
  input  [5:0] opcode,
  input  [3:0] func_4bit,
  output [9:0] ALU_OP
);

  wire and_2_out, and_3_out, and_4_out, and_5_out, and_6_out, and_7_out, and_9_out, and_10_out, and_11_out,
       and_12_out, and_13_out, and_14_out, and_15_out, and_17_out, and_18_out, and_19_out, and_20_out,
       and_21_out, and_22_out, and_23_out, not_1_out, not_2_out, not_3_out, not_4_out, not_5_out, not_7_out,
       not_8_out, not_9_out, not_10_out, or_1_out;
  wire [3:0] controlled_buffer_1_out;
  wire [8:0] or_7_out;
  wire [9:1] and_24_out;

  or or_1 (or_1_out, opcode[5], opcode[4], opcode[3], opcode[2], opcode[1], opcode[0]);
  not not_1 (not_1_out, or_1_out);
  assign controlled_buffer_1_out = not_1_out ? func_4bit : 4'bz;  // Controlled_Buffer controlled_buffer_1
  not not_2 (not_2_out, opcode[4]);
  not not_3 (not_3_out, opcode[3]);
  not not_4 (not_4_out, opcode[2]);
  not not_5 (not_5_out, opcode[1]);
  not not_6 (or_7_out[3], opcode[0]);
  not not_7 (not_7_out, controlled_buffer_1_out[3]);
  not not_8 (not_8_out, controlled_buffer_1_out[2]);
  not not_9 (not_9_out, controlled_buffer_1_out[1]);
  not not_10 (not_10_out, controlled_buffer_1_out[0]);
  and and_1 (or_7_out[8], opcode[2], or_7_out[3]);
  and and_2 (and_2_out, opcode[2], or_7_out[3]);
  and and_3 (and_3_out, opcode[4], opcode[1]);
  and and_4 (and_4_out, not_4_out, not_5_out);
  and and_5 (and_5_out, not_4_out, or_7_out[3]);
  and and_6 (and_6_out, opcode[1], opcode[0]);
  and and_7 (and_7_out, not_5_out, or_7_out[3]);
  and and_8 (or_7_out[2], not_2_out, not_4_out, not_5_out, or_7_out[3]);
  and and_9 (and_9_out, opcode[4], opcode[2]);
  and and_10 (and_10_out, opcode[2], opcode[1]);
  and and_11 (and_11_out, not_2_out, not_3_out, not_4_out);
  and and_12 (and_12_out, opcode[4], opcode[2], not_5_out);
  and and_13 (and_13_out, not_2_out, not_3_out, or_7_out[3]);
  and and_14 (and_14_out, controlled_buffer_1_out[3], not_8_out, not_9_out, not_10_out);
  and and_15 (and_15_out, controlled_buffer_1_out[3], controlled_buffer_1_out[2], controlled_buffer_1_out[0]);
  and and_16 (and_24_out[8], controlled_buffer_1_out[2], controlled_buffer_1_out[1]);
  and and_17 (and_17_out, not_7_out, not_8_out);
  and and_18 (and_18_out, controlled_buffer_1_out[3], controlled_buffer_1_out[2], controlled_buffer_1_out[0]);
  and and_19 (and_19_out, not_7_out, controlled_buffer_1_out[1], not_10_out);
  and and_20 (and_20_out, not_8_out, not_9_out);
  and and_21 (and_21_out, not_8_out, not_10_out);
  and and_22 (and_22_out, not_7_out, controlled_buffer_1_out[0]);
  and and_23 (and_23_out, controlled_buffer_1_out[3], controlled_buffer_1_out[2]);
  and and_24 (and_24_out[1], controlled_buffer_1_out[3], controlled_buffer_1_out[2]);
  or or_2 (or_7_out[7], and_2_out, and_3_out);
  or or_3 (or_7_out[6], not_3_out, and_4_out);
  or or_4 (or_7_out[5], not_3_out, and_5_out);
  or or_5 (or_7_out[4], and_6_out, and_7_out);
  or or_6 (or_7_out[1], and_9_out, and_10_out);
  or or_7 (or_7_out[0], and_11_out, and_12_out, and_13_out);
  or or_8 (and_24_out[9], and_14_out, and_15_out);
  or or_9 (and_24_out[7], and_17_out, and_18_out, and_19_out);
  or or_10 (and_24_out[4], not_7_out, and_20_out);
  or or_11 (and_24_out[3], not_7_out, and_21_out);
  or or_12 (and_24_out[2], and_22_out, and_23_out);
  Multiplexer #(.width(10)) multiplexer_1 (
    .in0({opcode[1], or_7_out}),
    .in1({and_24_out[9:7], controlled_buffer_1_out[1:0], and_24_out[4:1], controlled_buffer_1_out[0]}),
    .out(ALU_OP), .sel(not_1_out));  // open: en
endmodule
