// Logisim project ex_mem.circ as structural Verilog: 2 circuits, main circuit main
module main (
  input  in_1,
  input  WB,
  input  MEM_Read,
  input  MEM_Write,
  input  Reg_write,
  input  [1:0] Rd_src,
  input  [19:0] PC_plus_1,
  input  [4:0] Rd,
  input  [31:0] Alu_res,
  input  [15:0] imm16_16bit_EX,
  input  [31:0] imm16_32_EX,
  input  [31:0] BUSB_EX,
  input  SSET,
  input  zero_flag,
  input  Less_flag,
  input  less_flag_unsign,
  output out_17,
  output out_18,
  output out_19,
  output out_20,
  output [1:0] out_21,
  output [19:0] out_22,
  output [4:0] out_23,
  output [31:0] out_24,
  output [15:0] out_25,
  output [31:0] out_26,
  output [31:0] out_27,
  output out_28,
  output out_29,
  output out_30,
  output out_31
);

  Register #(.width(1)) register_1 (.D(WB), .en(1'b1), .clk(in_1), .Q(out_17));  // open: clr
  Register #(.width(1)) register_2 (.D(MEM_Read), .en(1'b1), .clk(in_1), .Q(out_18));  // open: clr
  Register #(.width(1)) register_3 (.D(MEM_Write), .en(1'b1), .clk(in_1), .Q(out_19));  // open: clr
  Register #(.width(1)) register_4 (.D(Reg_write), .en(1'b1), .clk(in_1), .Q(out_20));  // open: clr
  Register #(.width(2)) register_5 (.D(Rd_src), .en(1'b1), .clk(in_1), .Q(out_21));  // open: clr
  Register #(.width(20)) register_6 (.D(PC_plus_1), .en(1'b1), .clk(in_1), .Q(out_22));  // open: clr
  Register #(.width(5)) register_7 (.D(Rd), .en(1'b1), .clk(in_1), .Q(out_23));  // open: clr
  Register #(.width(32)) register_8 (.D(Alu_res), .en(1'b1), .clk(in_1), .Q(out_24));  // open: clr
  Register #(.width(16)) register_9 (.D(imm16_16bit_EX), .en(1'b1), .clk(in_1), .Q(out_25));  // open: clr
  Register #(.width(32)) register_10 (.D(imm16_32_EX), .en(1'b1), .clk(in_1), .Q(out_26));  // open: clr
  Register #(.width(32)) register_11 (.D(BUSB_EX), .en(1'b1), .clk(in_1), .Q(out_27));  // open: clr
  Register #(.width(1)) register_12 (.D(SSET), .en(1'b1), .clk(in_1), .Q(out_28));  // open: clr
  Register #(.width(1)) register_13 (.D(zero_flag), .en(1'b1), .clk(in_1), .Q(out_29));  // open: clr
  Register #(.width(1)) register_14 (.D(Less_flag), .en(1'b1), .clk(in_1), .Q(out_30));  // open: clr
  Register #(.width(1)) register_15 (.D(less_flag_unsign), .en(1'b1), .clk(in_1), .Q(out_31));  // open: clr

  // Other names for the same wires on the sheet: CLk = in_1

  // Notes on the sheet:
  //   WB
  //   Mem_read
  //   mem_Write
  //   reg_wreite
  //   Rd_src
  //   pc+1
  //   Rd
  //   bus B
  //   alu_res
endmodule

module block (
);

  main main_1 ();  // open: in_1, WB, MEM_Read, MEM_Write, Reg_write, Rd_src, PC_plus_1, Rd, Alu_res, out_17, out_18, out_19, out_20, out_21, out_22, out_23, out_24, imm16_16bit_EX, out_25, imm16_32_EX, out_26, BUSB_EX, out_27, SSET, out_28, zero_flag, out_29, Less_flag, out_30, less_flag_unsign, out_31
endmodule
