// Logisim project id_ex.circ as structural Verilog: 2 circuits, main circuit main
module main (
  input  in_1,
  input  [31:0] imm16,
  input  [4:0] ImmL,
  input  [10:0] ImmU,
  input  [31:0] BusA,
  input  [31:0] BusB,
  input  [4:0] Rs,
  input  [4:0] Rt,
  input  [19:0] PC_plus_1,
  input  MEM_Read,
  input  MEM_Write,
  input  WB,
  input  Reg_Write,
  input  [1:0] Reg_Des,
  input  [4:0] RD,
  input  [9:0] ALU_OP,
  input  [1:0] ALU_SRC,
  input  SSET,
  input  [19:0] PC,
  output [31:0] out_20,
  output [4:0] out_21,
  output [10:0] out_22,
  output [31:0] out_23,
  output [31:0] out_24,
  output [4:0] out_25,
  output [4:0] out_26,
  output [19:0] out_27,
  output out_28,
  output out_29,
  output out_30,
  output out_31,
  output [1:0] out_32,
  output [4:0] out_33,
  output [9:0] out_34,
  output [1:0] out_35,
  output out_36,
  output [19:0] out_37
);

  Register #(.width(32)) register_1 (.D(imm16), .en(1'b1), .clk(in_1), .Q(out_20));  // open: clr
  Register #(.width(5)) register_2 (.D(ImmL), .en(1'b1), .clk(in_1), .Q(out_21));  // open: clr
  Register #(.width(11)) register_3 (.D(ImmU), .en(1'b1), .clk(in_1), .Q(out_22));  // open: clr
  Register #(.width(32)) register_4 (.D(BusA), .en(1'b1), .clk(in_1), .Q(out_23));  // open: clr
  Register #(.width(32)) register_5 (.D(BusB), .en(1'b1), .clk(in_1), .Q(out_24));  // open: clr
  Register #(.width(5)) register_6 (.D(Rs), .en(1'b1), .clk(in_1), .Q(out_25));  // open: clr
  Register #(.width(5)) register_7 (.D(Rt), .en(1'b1), .clk(in_1), .Q(out_26));  // open: clr
  Register #(.width(20)) register_8 (.D(PC_plus_1), .en(1'b1), .clk(in_1), .Q(out_27));  // open: clr
  Register #(.width(1)) register_9 (.D(MEM_Read), .en(1'b1), .clk(in_1), .Q(out_28));  // open: clr
  Register #(.width(1)) register_10 (.D(MEM_Write), .en(1'b1), .clk(in_1), .Q(out_29));  // open: clr
  Register #(.width(1)) register_11 (.D(WB), .en(1'b1), .clk(in_1), .Q(out_30));  // open: clr
  Register #(.width(1)) register_12 (.D(Reg_Write), .en(1'b1), .clk(in_1), .Q(out_31));  // open: clr
  Register #(.width(2)) register_13 (.D(Reg_Des), .en(1'b1), .clk(in_1), .Q(out_32));  // open: clr
  Register #(.width(5)) register_14 (.D(RD), .en(1'b1), .clk(in_1), .Q(out_33));  // open: clr
  Register #(.width(10)) register_15 (.D(ALU_OP), .en(1'b1), .clk(in_1), .Q(out_34));  // open: clr
  Register #(.width(2)) register_16 (.D(ALU_SRC), .en(1'b1), .clk(in_1), .Q(out_35));  // open: clr
  Register #(.width(1)) register_17 (.D(SSET), .en(1'b1), .clk(in_1), .Q(out_36));  // open: clr
  Register #(.width(20)) register_18 (.D(PC), .en(1'b1), .clk(in_1), .Q(out_37));  // open: clr

  // Other names for the same wires on the sheet: ClK = in_1

  // Notes on the sheet:
  //   imm16
  //   imml/imml
  //   busA
  //   bysb
  //   rs
  //   rt
  //   rd
  //   pc+1
  //   memread
  //   memwriete
  //   wb
  //   regwrite
  //   regdest
endmodule

module block (
);

  main main_1 ();  // open: in_1, imm16, BusA, BusB, Rs, Rt, PC_plus_1, MEM_Read, MEM_Write, WB, Reg_Write, Reg_Des, RD, out_20, out_23, out_24, out_25, out_26, out_27, out_28, out_29, out_30, out_31, out_32, out_33, ALU_OP, out_34, ALU_SRC, out_35, ImmL, out_21, ImmU, out_22, SSET, out_36, PC, out_37
endmodule
