// Logisim project if_id.circ as structural Verilog: 2 circuits, main circuit main
module main (
  input  [31:0] Instruction,
  input  [19:0] PC_plus_1,
  input  [19:0] PC,
  input  stall,
  input  in_5,
  output [31:0] out_6,
  output [19:0] out_7,
  output [19:0] out_8
);

  wire not_1_out;

  not not_1 (not_1_out, stall);
  Register #(.width(32)) register_1 (.D(Instruction), .en(not_1_out), .clk(in_5), .Q(out_6));  // open: clr
  Register #(.width(20)) register_2 (.D(PC_plus_1), .en(not_1_out), .clk(in_5), .Q(out_7));  // open: clr
  Register #(.width(20)) register_3 (.D(PC), .en(not_1_out), .clk(in_5), .Q(out_8));  // open: clr
endmodule

module block (
);

  main main_1 ();  // open: Instruction, PC_plus_1, out_6, out_7, in_5, stall, PC, out_8
endmodule
