// Logisim project is_branch.circ as structural Verilog: 2 circuits, main circuit main
module main (
  input  [4:0] in_1,
  output out_2
);

  wire decoder_1_out18, decoder_1_out19, decoder_1_out20, decoder_1_out21, decoder_1_out22, decoder_1_out23;

  Decoder #(.select(5)) decoder_1 (
    .out18(decoder_1_out18), .out19(decoder_1_out19), .out20(decoder_1_out20), .out21(decoder_1_out21),
    .out22(decoder_1_out22), .out23(decoder_1_out23), .sel(in_1));  // open: out0, out1, out2, out3, out4, out5, out6, out7, out8, out9, out10, out11, out12, out13, out14, out15, out16, out17, out24, out25, out26, out27, out28, out29, out30, out31, en
  or or_1 (out_2, decoder_1_out18, decoder_1_out19, decoder_1_out20, decoder_1_out21, decoder_1_out22, decoder_1_out23);
endmodule

module block (
);

  main main_1 ();  // open: in_1, out_2
endmodule
