// Logisim project main_contr_unit.circ as structural Verilog
module main_control_unit (
  input  [5:0] opcode,
  input  Stall,
  output reg_write,
  output ext_op,
  output [1:0] Rd_src,
  output [1:0] alu_src,
  output mem_write,
  output mem_read,
  output wb,
  output out_10
);

  wire and_1_out, and_2_out, and_4_out, and_5_out, and_6_out, and_7_out, and_8_out, and_9_out, and_10_out,
       and_13_out, and_14_out, and_15_out, and_16_out, and_17_out, and_23_out, not_1_out, not_2_out,
       not_3_out, not_4_out, not_5_out, not_6_out, not_7_out, not_8_out, not_9_out, or_2_out;
  wire [1:0] and_3_out, and_11_out, bit_extender_1_out, or_5_out;

  not not_1 (not_1_out, opcode[4]);
  not not_2 (not_2_out, opcode[3]);
  not not_3 (not_3_out, opcode[2]);
  not not_4 (not_4_out, opcode[1]);
  not not_5 (not_5_out, opcode[0]);
  and and_1 (and_1_out, opcode[4], opcode[1]);
  and and_2 (and_2_out, opcode[4], opcode[2]);
  and and_3 (and_3_out[0], opcode[3], opcode[2], opcode[1], opcode[0]);
  and and_4 (and_4_out, not_3_out, not_4_out, not_5_out);
  and and_5 (and_5_out, opcode[1], opcode[0]);
  and and_6 (and_6_out, not_3_out, opcode[0]);
  and and_7 (and_7_out, opcode[3], opcode[2], not_5_out);
  and and_8 (and_8_out, opcode[3], opcode[1]);
  and and_9 (and_9_out, not_4_out, not_5_out);
  and and_10 (and_10_out, opcode[1], opcode[0]);
  and and_11 (and_11_out[0], opcode[3], opcode[2], opcode[0]);
  and and_12 (or_5_out[1], opcode[4], not_3_out, not_4_out, opcode[0]);
  and and_13 (and_13_out, not_1_out, not_2_out, not_3_out, not_4_out, not_5_out);
  and and_14 (and_14_out, opcode[4], opcode[1]);
  and and_15 (and_15_out, opcode[4], opcode[2]);
  and and_16 (and_16_out, opcode[4], not_3_out, not_4_out, not_5_out);
  and and_17 (and_17_out, opcode[4], not_3_out, not_4_out, opcode[0]);
  or or_1 (and_3_out[1], and_1_out, and_2_out);
  or or_2 (or_2_out, not_1_out, and_4_out);
  or or_3 (ext_op, and_5_out, and_6_out, and_7_out, and_8_out);
  or or_4 (and_11_out[1], not_2_out, not_3_out, and_9_out, and_10_out);
  or or_5 (or_5_out[0], and_13_out, and_14_out, and_15_out);
  not not_6 (not_6_out, Stall);
  and and_18 (reg_write, or_2_out, not_6_out);
  assign bit_extender_1_out = {{1{not_6_out}}, not_6_out};  // Bit_Extender bit_extender_1
  and and_19 (mem_write, and_16_out, not_6_out);
  and and_20 (mem_read, and_17_out, not_6_out);
  and and_21 (wb, opcode[4], not_6_out);
  not not_7 (not_7_out, opcode[4]);
  not not_8 (not_8_out, opcode[0]);
  not not_9 (not_9_out, opcode[5]);
  assign Rd_src = and_11_out & bit_extender_1_out;  // AND_Gate and_22, 2 bits wide
  and and_23 (and_23_out, not_8_out, opcode[1], opcode[2], opcode[3], not_7_out, not_9_out);
  assign alu_src = or_5_out & bit_extender_1_out;  // AND_Gate and_24, 2 bits wide
  and and_25 (out_10, opcode[3], and_23_out);

  // Other names for the same wires on the sheet: sss = opcode[3]
endmodule

module Main_Control_Block (
);

  main_control_unit main_control_unit_1 ();  // open: opcode, reg_write, ext_op, Rd_src, alu_src, mem_write, mem_read, wb, Stall, out_10
endmodule
