// Logisim project mem_wb.circ as structural Verilog: 2 circuits, main circuit main
module main (
  input  [31:0] ALUres_or_DataOut,
  input  reg_write,
  input  [1:0] rd_src,
  input  [19:0] PC_Plus_1,
  input  [4:0] rd,
  input  [15:0] imm16_16bit_mem,
  input  [31:0] imm16_32_mem,
  input  [31:0] BUSB_mem,
  input  SSET,
  input  clk,
  output [31:0] out_11,
  output out_12,
  output [1:0] out_13,
  output [19:0] out_14,
  output [4:0] out_15,
  output [15:0] out_16,
  output [31:0] out_17,
  output [31:0] out_18,
  output out_19
);

  Register #(.width(32)) register_1 (.D(ALUres_or_DataOut), .en(1'b1), .clk(clk), .Q(out_11));  // open: clr
  Register #(.width(1)) register_2 (.D(reg_write), .en(1'b1), .clk(clk), .Q(out_12));  // open: clr
  Register #(.width(2)) register_3 (.D(rd_src), .en(1'b1), .clk(clk), .Q(out_13));  // open: clr
  Register #(.width(20)) register_4 (.D(PC_Plus_1), .en(1'b1), .clk(clk), .Q(out_14));  // open: clr
  Register #(.width(5)) register_5 (.D(rd), .en(1'b1), .clk(clk), .Q(out_15));  // open: clr
  Register #(.width(16)) register_6 (.D(imm16_16bit_mem), .en(1'b1), .clk(clk), .Q(out_16));  // open: clr
  Register #(.width(32)) register_7 (.D(imm16_32_mem), .en(1'b1), .clk(clk), .Q(out_17));  // open: clr
  Register #(.width(32)) register_8 (.D(BUSB_mem), .en(1'b1), .clk(clk), .Q(out_18));  // open: clr
  Register #(.width(1)) register_9 (.D(SSET), .en(1'b1), .clk(clk), .Q(out_19));  // open: clr

  // Notes on the sheet:
  //   WB
  //   reg_write
  //   rd_src
  //   PC_plus_1
  //   rd
endmodule

module bllock (
);

  main main_1 ();  // open: reg_write, rd_src, PC_Plus_1, rd, clk, out_12, out_13, out_14, out_15, ALUres_or_DataOut, out_11, imm16_16bit_mem, out_16, imm16_32_mem, out_17, BUSB_mem, out_18, SSET, out_19
endmodule
