// Logisim project regfile_new.circ as structural Verilog: 2 circuits, main circuit main
module main (
  input  [4:0] Ra,
  input  [4:0] Rb,
  input  [4:0] Rw,
  input  Clk,
  input  Reg_write,
  input  [31:0] Bus_W,
  output [31:0] R0,
  output [31:0] R1,
  output [31:0] R2,
  output [31:0] R3,
  output [31:0] R4,
  output [31:0] R5,
  output [31:0] R6,
  output [31:0] R7,
  output [31:0] R8,
  output [31:0] R9,
  output [31:0] R10,
  output [31:0] R11,
  output [31:0] R12,
  output [31:0] R13,
  output [31:0] R14,
  output [31:0] R15,
  output [31:0] R16,
  output [31:0] R17,
  output [31:0] R18,
  output [31:0] R19,
  output [31:0] R20,
  output [31:0] R21,
  output [31:0] R22,
  output [31:0] R23,
  output [31:0] R24,
  output [31:0] R25,
  output [31:0] R26,
  output [31:0] R27,
  output [31:0] R28,
  output [31:0] R29,
  output [31:0] R30,
  output [31:0] R31,
  output [31:0] Bus_A,
  output [31:0] Bus_B
);

  wire and_1_out, and_2_out, and_3_out, and_4_out, and_5_out, and_6_out, and_7_out, and_8_out, and_9_out,
       and_10_out, and_11_out, and_12_out, and_13_out, and_14_out, and_15_out, and_16_out, and_17_out,
       and_18_out, and_19_out, and_20_out, and_21_out, and_22_out, and_23_out, and_24_out, and_25_out,
       and_26_out, and_27_out, and_28_out, and_29_out, and_30_out, and_31_out, decoder_1_out0,
       decoder_1_out1, decoder_1_out2, decoder_1_out3, decoder_1_out4, decoder_1_out5, decoder_1_out6,
       decoder_1_out7, decoder_1_out8, decoder_1_out9, decoder_1_out10, decoder_1_out11, decoder_1_out12,
       decoder_1_out13, decoder_1_out14, decoder_1_out15, decoder_1_out16, decoder_1_out17, decoder_1_out18,
       decoder_1_out19, decoder_1_out20, decoder_1_out21, decoder_1_out22, decoder_1_out23, decoder_1_out24,
       decoder_1_out25, decoder_1_out26, decoder_1_out27, decoder_1_out28, decoder_1_out29, decoder_1_out30,
       decoder_1_out31, decoder_2_out0, decoder_2_out1, decoder_2_out2, decoder_2_out3, decoder_2_out4,
       decoder_2_out5, decoder_2_out6, decoder_2_out7, decoder_2_out8, decoder_2_out9, decoder_2_out10,
       decoder_2_out11, decoder_2_out12, decoder_2_out13, decoder_2_out14, decoder_2_out15, decoder_2_out16,
       decoder_2_out17, decoder_2_out18, decoder_2_out19, decoder_2_out20, decoder_2_out21, decoder_2_out22,
       decoder_2_out23, decoder_2_out24, decoder_2_out25, decoder_2_out26, decoder_2_out27, decoder_2_out28,
       decoder_2_out29, decoder_2_out30, decoder_2_out31, decoder_3_out0, decoder_3_out1, decoder_3_out2,
       decoder_3_out3, decoder_3_out4, decoder_3_out5, decoder_3_out6, decoder_3_out7, decoder_3_out8,
       decoder_3_out9, decoder_3_out10, decoder_3_out11, decoder_3_out12, decoder_3_out13, decoder_3_out14,
       decoder_3_out15, decoder_3_out16, decoder_3_out17, decoder_3_out18, decoder_3_out19, decoder_3_out20,
       decoder_3_out21, decoder_3_out22, decoder_3_out23, decoder_3_out24, decoder_3_out25, decoder_3_out26,
       decoder_3_out27, decoder_3_out28, decoder_3_out29, decoder_3_out30, decoder_3_out31;

  Decoder #(.select(5), .enable("false")) decoder_1 (
    .out0(decoder_1_out0), .out1(decoder_1_out1), .out2(decoder_1_out2), .out3(decoder_1_out3),
    .out4(decoder_1_out4), .out5(decoder_1_out5), .out6(decoder_1_out6), .out7(decoder_1_out7),
    .out8(decoder_1_out8), .out9(decoder_1_out9), .out10(decoder_1_out10), .out11(decoder_1_out11),
    .out12(decoder_1_out12), .out13(decoder_1_out13), .out14(decoder_1_out14), .out15(decoder_1_out15),
    .out16(decoder_1_out16), .out17(decoder_1_out17), .out18(decoder_1_out18), .out19(decoder_1_out19),
    .out20(decoder_1_out20), .out21(decoder_1_out21), .out22(decoder_1_out22), .out23(decoder_1_out23),
    .out24(decoder_1_out24), .out25(decoder_1_out25), .out26(decoder_1_out26), .out27(decoder_1_out27),
    .out28(decoder_1_out28), .out29(decoder_1_out29), .out30(decoder_1_out30), .out31(decoder_1_out31),
    .sel(Rw));
  and and_1 (and_1_out, decoder_1_out1, Reg_write);
  and and_2 (and_2_out, decoder_1_out2, Reg_write);
  and and_3 (and_3_out, decoder_1_out3, Reg_write);
  and and_4 (and_4_out, decoder_1_out4, Reg_write);
  and and_5 (and_5_out, decoder_1_out5, Reg_write);
  and and_6 (and_6_out, decoder_1_out6, Reg_write);
  and and_7 (and_7_out, decoder_1_out7, Reg_write);
  and and_8 (and_8_out, decoder_1_out8, Reg_write);
  and and_9 (and_9_out, decoder_1_out9, Reg_write);
  and and_10 (and_10_out, decoder_1_out10, Reg_write);
  and and_11 (and_11_out, decoder_1_out11, Reg_write);
  and and_12 (and_12_out, decoder_1_out12, Reg_write);
  and and_13 (and_13_out, decoder_1_out13, Reg_write);
  and and_14 (and_14_out, decoder_1_out14, Reg_write);
  and and_15 (and_15_out, decoder_1_out15, Reg_write);
  and and_16 (and_16_out, decoder_1_out16, Reg_write);
  and and_17 (and_17_out, decoder_1_out17, Reg_write);
  and and_18 (and_18_out, decoder_1_out18, Reg_write);
  and and_19 (and_19_out, decoder_1_out19, Reg_write);
  and and_20 (and_20_out, decoder_1_out20, Reg_write);
  and and_21 (and_21_out, decoder_1_out21, Reg_write);
  and and_22 (and_22_out, decoder_1_out22, Reg_write);
  and and_23 (and_23_out, decoder_1_out23, Reg_write);
  and and_24 (and_24_out, decoder_1_out24, Reg_write);
  and and_25 (and_25_out, decoder_1_out25, Reg_write);
  and and_26 (and_26_out, decoder_1_out26, Reg_write);
  and and_27 (and_27_out, decoder_1_out27, Reg_write);
  and and_28 (and_28_out, decoder_1_out28, Reg_write);
  and and_29 (and_29_out, decoder_1_out29, Reg_write);
  and and_30 (and_30_out, decoder_1_out30, Reg_write);
  and and_31 (and_31_out, decoder_1_out31, Reg_write);
  Register #(.width(32)) u_R1 (.D(Bus_W), .en(and_1_out), .clk(Clk), .Q(R1));  // open: clr
  Register #(.width(32)) u_R2 (.D(Bus_W), .en(and_2_out), .clk(Clk), .Q(R2));  // open: clr
  Register #(.width(32)) u_R3 (.D(Bus_W), .en(and_3_out), .clk(Clk), .Q(R3));  // open: clr
  Register #(.width(32)) u_R4 (.D(Bus_W), .en(and_4_out), .clk(Clk), .Q(R4));  // open: clr
  Register #(.width(32)) u_R5 (.D(Bus_W), .en(and_5_out), .clk(Clk), .Q(R5));  // open: clr
  Register #(.width(32)) u_R6 (.D(Bus_W), .en(and_6_out), .clk(Clk), .Q(R6));  // open: clr
  Register #(.width(32)) u_R7 (.D(Bus_W), .en(and_7_out), .clk(Clk), .Q(R7));  // open: clr
  Register #(.width(32)) u_R8 (.D(Bus_W), .en(and_8_out), .clk(Clk), .Q(R8));  // open: clr
  Register #(.width(32)) u_R9 (.D(Bus_W), .en(and_9_out), .clk(Clk), .Q(R9));  // open: clr
  Register #(.width(32)) u_R10 (.D(Bus_W), .en(and_10_out), .clk(Clk), .Q(R10));  // open: clr
  Register #(.width(32)) u_R11 (.D(Bus_W), .en(and_11_out), .clk(Clk), .Q(R11));  // open: clr
  Register #(.width(32)) u_R12 (.D(Bus_W), .en(and_12_out), .clk(Clk), .Q(R12));  // open: clr
  Register #(.width(32)) u_R13 (.D(Bus_W), .en(and_13_out), .clk(Clk), .Q(R13));  // open: clr
  Register #(.width(32)) u_R14 (.D(Bus_W), .en(and_14_out), .clk(Clk), .Q(R14));  // open: clr
  Register #(.width(32)) u_R15 (.D(Bus_W), .en(and_15_out), .clk(Clk), .Q(R15));  // open: clr
  Register #(.width(32)) u_R16 (.D(Bus_W), .en(and_16_out), .clk(Clk), .Q(R16));  // open: clr
  Register #(.width(32)) u_R17 (.D(Bus_W), .en(and_17_out), .clk(Clk), .Q(R17));  // open: clr
  Register #(.width(32)) u_R18 (.D(Bus_W), .en(and_18_out), .clk(Clk), .Q(R18));  // open: clr
  Register #(.width(32)) u_R19 (.D(Bus_W), .en(and_19_out), .clk(Clk), .Q(R19));  // open: clr
  Register #(.width(32)) u_R20 (.D(Bus_W), .en(and_20_out), .clk(Clk), .Q(R20));  // open: clr
  Register #(.width(32)) u_R21 (.D(Bus_W), .en(and_21_out), .clk(Clk), .Q(R21));  // open: clr
  Register #(.width(32)) u_R22 (.D(Bus_W), .en(and_22_out), .clk(Clk), .Q(R22));  // open: clr
  Register #(.width(32)) u_R23 (.D(Bus_W), .en(and_23_out), .clk(Clk), .Q(R23));  // open: clr
  Register #(.width(32)) u_R24 (.D(Bus_W), .en(and_24_out), .clk(Clk), .Q(R24));  // open: clr
  Register #(.width(32)) u_R25 (.D(Bus_W), .en(and_25_out), .clk(Clk), .Q(R25));  // open: clr
  Register #(.width(32)) u_R26 (.D(Bus_W), .en(and_26_out), .clk(Clk), .Q(R26));  // open: clr
  Register #(.width(32)) u_R27 (.D(Bus_W), .en(and_27_out), .clk(Clk), .Q(R27));  // open: clr
  Register #(.width(32)) u_R28 (.D(Bus_W), .en(and_28_out), .clk(Clk), .Q(R28));  // open: clr
  Register #(.width(32)) u_R29 (.D(Bus_W), .en(and_29_out), .clk(Clk), .Q(R29));  // open: clr
  Register #(.width(32)) u_R30 (.D(Bus_W), .en(and_30_out), .clk(Clk), .Q(R30));  // open: clr
  Register #(.width(32)) u_R31 (.D(Bus_W), .en(and_31_out), .clk(Clk), .Q(R31));  // open: clr
  assign Bus_A = decoder_2_out1 ? R1 : 32'bz;  // Controlled_Buffer controlled_buffer_1
  Decoder #(.select(5)) decoder_2 (
    .out0(decoder_2_out0), .out1(decoder_2_out1), .out2(decoder_2_out2), .out3(decoder_2_out3),
    .out4(decoder_2_out4), .out5(decoder_2_out5), .out6(decoder_2_out6), .out7(decoder_2_out7),
    .out8(decoder_2_out8), .out9(decoder_2_out9), .out10(decoder_2_out10), .out11(decoder_2_out11),
    .out12(decoder_2_out12), .out13(decoder_2_out13), .out14(decoder_2_out14), .out15(decoder_2_out15),
    .out16(decoder_2_out16), .out17(decoder_2_out17), .out18(decoder_2_out18), .out19(decoder_2_out19),
    .out20(decoder_2_out20), .out21(decoder_2_out21), .out22(decoder_2_out22), .out23(decoder_2_out23),
    .out24(decoder_2_out24), .out25(decoder_2_out25), .out26(decoder_2_out26), .out27(decoder_2_out27),
    .out28(decoder_2_out28), .out29(decoder_2_out29), .out30(decoder_2_out30), .out31(decoder_2_out31),
    .sel(Ra));  // open: en
  assign Bus_A = decoder_2_out2 ? R2 : 32'bz;  // Controlled_Buffer controlled_buffer_2
  assign Bus_A = decoder_2_out3 ? R3 : 32'bz;  // Controlled_Buffer controlled_buffer_3
  assign Bus_A = decoder_2_out4 ? R4 : 32'bz;  // Controlled_Buffer controlled_buffer_4
  assign Bus_A = decoder_2_out5 ? R5 : 32'bz;  // Controlled_Buffer controlled_buffer_5
  assign Bus_A = decoder_2_out6 ? R6 : 32'bz;  // Controlled_Buffer controlled_buffer_6
  assign Bus_A = decoder_2_out7 ? R7 : 32'bz;  // Controlled_Buffer controlled_buffer_7
  assign Bus_A = decoder_2_out8 ? R8 : 32'bz;  // Controlled_Buffer controlled_buffer_8
  assign Bus_A = decoder_2_out9 ? R9 : 32'bz;  // Controlled_Buffer controlled_buffer_9
  assign Bus_A = decoder_2_out10 ? R10 : 32'bz;  // Controlled_Buffer controlled_buffer_10
  assign Bus_A = decoder_2_out11 ? R11 : 32'bz;  // Controlled_Buffer controlled_buffer_11
  assign Bus_A = decoder_2_out12 ? R12 : 32'bz;  // Controlled_Buffer controlled_buffer_12
  assign Bus_A = decoder_2_out13 ? R13 : 32'bz;  // Controlled_Buffer controlled_buffer_13
  assign Bus_A = decoder_2_out14 ? R14 : 32'bz;  // Controlled_Buffer controlled_buffer_14
  assign Bus_A = decoder_2_out15 ? R15 : 32'bz;  // Controlled_Buffer controlled_buffer_15
  assign Bus_A = decoder_2_out16 ? R16 : 32'bz;  // Controlled_Buffer controlled_buffer_16
  assign Bus_A = decoder_2_out17 ? R17 : 32'bz;  // Controlled_Buffer controlled_buffer_17
  assign Bus_A = decoder_2_out18 ? R18 : 32'bz;  // Controlled_Buffer controlled_buffer_18
  assign Bus_A = decoder_2_out19 ? R19 : 32'bz;  // Controlled_Buffer controlled_buffer_19
  assign Bus_A = decoder_2_out20 ? R20 : 32'bz;  // Controlled_Buffer controlled_buffer_20
  assign Bus_A = decoder_2_out21 ? R21 : 32'bz;  // Controlled_Buffer controlled_buffer_21
  assign Bus_A = decoder_2_out22 ? R22 : 32'bz;  // Controlled_Buffer controlled_buffer_22
  assign Bus_A = decoder_2_out23 ? R23 : 32'bz;  // Controlled_Buffer controlled_buffer_23
  assign Bus_A = decoder_2_out24 ? R24 : 32'bz;  // Controlled_Buffer controlled_buffer_24
  assign Bus_A = decoder_2_out25 ? R25 : 32'bz;  // Controlled_Buffer controlled_buffer_25
  assign Bus_A = decoder_2_out26 ? R26 : 32'bz;  // Controlled_Buffer controlled_buffer_26
  assign Bus_A = decoder_2_out27 ? R27 : 32'bz;  // Controlled_Buffer controlled_buffer_27
  assign Bus_A = decoder_2_out28 ? R28 : 32'bz;  // Controlled_Buffer controlled_buffer_28
  assign Bus_A = decoder_2_out29 ? R29 : 32'bz;  // Controlled_Buffer controlled_buffer_29
  assign Bus_A = decoder_2_out30 ? R30 : 32'bz;  // Controlled_Buffer controlled_buffer_30
  assign Bus_A = decoder_2_out31 ? R31 : 32'bz;  // Controlled_Buffer controlled_buffer_31
  assign Bus_A = decoder_2_out0 ? {32{1'b0}} : 32'bz;  // Controlled_Buffer controlled_buffer_32
  assign Bus_B = decoder_3_out0 ? {32{1'b0}} : 32'bz;  // Controlled_Buffer controlled_buffer_33
  assign Bus_B = decoder_3_out1 ? R1 : 32'bz;  // Controlled_Buffer controlled_buffer_34
  assign Bus_B = decoder_3_out2 ? R2 : 32'bz;  // Controlled_Buffer controlled_buffer_35
  assign Bus_B = decoder_3_out3 ? R3 : 32'bz;  // Controlled_Buffer controlled_buffer_36
  assign Bus_B = decoder_3_out4 ? R4 : 32'bz;  // Controlled_Buffer controlled_buffer_37
  assign Bus_B = decoder_3_out5 ? R5 : 32'bz;  // Controlled_Buffer controlled_buffer_38
  assign Bus_B = decoder_3_out6 ? R6 : 32'bz;  // Controlled_Buffer controlled_buffer_39
  assign Bus_B = decoder_3_out7 ? R7 : 32'bz;  // Controlled_Buffer controlled_buffer_40
  assign Bus_B = decoder_3_out8 ? R8 : 32'bz;  // Controlled_Buffer controlled_buffer_41
  assign Bus_B = decoder_3_out9 ? R9 : 32'bz;  // Controlled_Buffer controlled_buffer_42
  assign Bus_B = decoder_3_out10 ? R10 : 32'bz;  // Controlled_Buffer controlled_buffer_43
  assign Bus_B = decoder_3_out11 ? R11 : 32'bz;  // Controlled_Buffer controlled_buffer_44
  assign Bus_B = decoder_3_out12 ? R12 : 32'bz;  // Controlled_Buffer controlled_buffer_45
  assign Bus_B = decoder_3_out13 ? R13 : 32'bz;  // Controlled_Buffer controlled_buffer_46
  assign Bus_B = decoder_3_out14 ? R14 : 32'bz;  // Controlled_Buffer controlled_buffer_47
  assign Bus_B = decoder_3_out15 ? R15 : 32'bz;  // Controlled_Buffer controlled_buffer_48
  assign Bus_B = decoder_3_out16 ? R16 : 32'bz;  // Controlled_Buffer controlled_buffer_49
  assign Bus_B = decoder_3_out17 ? R17 : 32'bz;  // Controlled_Buffer controlled_buffer_50
  assign Bus_B = decoder_3_out18 ? R18 : 32'bz;  // Controlled_Buffer controlled_buffer_51
  assign Bus_B = decoder_3_out19 ? R19 : 32'bz;  // Controlled_Buffer controlled_buffer_52
  assign Bus_B = decoder_3_out20 ? R20 : 32'bz;  // Controlled_Buffer controlled_buffer_53
  assign Bus_B = decoder_3_out21 ? R21 : 32'bz;  // Controlled_Buffer controlled_buffer_54
  assign Bus_B = decoder_3_out22 ? R22 : 32'bz;  // Controlled_Buffer controlled_buffer_55
  assign Bus_B = decoder_3_out23 ? R23 : 32'bz;  // Controlled_Buffer controlled_buffer_56
  assign Bus_B = decoder_3_out24 ? R24 : 32'bz;  // Controlled_Buffer controlled_buffer_57
  assign Bus_B = decoder_3_out25 ? R25 : 32'bz;  // Controlled_Buffer controlled_buffer_58
  assign Bus_B = decoder_3_out26 ? R26 : 32'bz;  // Controlled_Buffer controlled_buffer_59
  assign Bus_B = decoder_3_out27 ? R27 : 32'bz;  // Controlled_Buffer controlled_buffer_60
  assign Bus_B = decoder_3_out28 ? R28 : 32'bz;  // Controlled_Buffer controlled_buffer_61
  assign Bus_B = decoder_3_out29 ? R29 : 32'bz;  // Controlled_Buffer controlled_buffer_62
  assign Bus_B = decoder_3_out30 ? R30 : 32'bz;  // Controlled_Buffer controlled_buffer_63
  assign Bus_B = decoder_3_out31 ? R31 : 32'bz;  // Controlled_Buffer controlled_buffer_64
  Decoder #(.select(5)) decoder_3 (
    .out0(decoder_3_out0), .out1(decoder_3_out1), .out2(decoder_3_out2), .out3(decoder_3_out3),
    .out4(decoder_3_out4), .out5(decoder_3_out5), .out6(decoder_3_out6), .out7(decoder_3_out7),
    .out8(decoder_3_out8), .out9(decoder_3_out9), .out10(decoder_3_out10), .out11(decoder_3_out11),
    .out12(decoder_3_out12), .out13(decoder_3_out13), .out14(decoder_3_out14), .out15(decoder_3_out15),
    .out16(decoder_3_out16), .out17(decoder_3_out17), .out18(decoder_3_out18), .out19(decoder_3_out19),
    .out20(decoder_3_out20), .out21(decoder_3_out21), .out22(decoder_3_out22), .out23(decoder_3_out23),
    .out24(decoder_3_out24), .out25(decoder_3_out25), .out26(decoder_3_out26), .out27(decoder_3_out27),
    .out28(decoder_3_out28), .out29(decoder_3_out29), .out30(decoder_3_out30), .out31(decoder_3_out31),
    .sel(Rb));  // open: en

  assign R0 = {32{1'b0}};

  // Notes on the sheet:
  //   Reg Write
  //   bus W
  //   bus A
  //   bus B
endmodule

module Register_file_Block (
);

  main main_1 ();  // open: Ra, Rb, Rw, Reg_write, Bus_W, Bus_A, Bus_B, Clk, R1, R2, R3, R4, R0, R5, R6, R7, R8, R9, R10, R11, R12, R13, R14, R15, R16, R17, R18, R19, R20, R21, R22, R23, R24, R25, R26, R27, R28, R29, R30, R31
endmodule
