// Logisim project v.circ as structural Verilog: 1 circuit, main circuit main
module main (
  output [31:0] out_1,
  output [31:0] out_2,
  output [31:0] out_3,
  output [31:0] out_4,
  output [31:0] out_5,
  output [31:0] out_6,
  output [31:0] out_7,
  output [31:0] out_8,
  output [31:0] out_9,
  output [31:0] out_10,
  output [31:0] out_11,
  output [31:0] out_12,
  output [31:0] out_13,
  output [31:0] out_14,
  output [31:0] out_15,
  output [31:0] out_16,
  output [31:0] out_17,
  output [31:0] out_18,
  output [31:0] out_19,
  output [31:0] out_20,
  output [31:0] out_21,
  output [31:0] out_22,
  output [31:0] out_23,
  output [31:0] out_24,
  output [31:0] out_25,
  output [31:0] out_26,
  output [31:0] out_27,
  output [31:0] out_28,
  output [31:0] out_29,
  output [31:0] out_30,
  output [31:0] out_31,
  output [31:0] out_32
);

  // Probe on out_1
  // Probe on out_15
  // Probe on out_29
  // Probe on out_2
  // Probe on out_16
  // Probe on out_30
  // Probe on out_3
  // Probe on out_17
  // Probe on out_31
  // Probe on out_4
  // Probe on out_18
  // Probe on out_32
  // Probe on out_5
  // Probe on out_19
  // Probe on out_6
  // Probe on out_7
  // Probe on out_20
  // Probe on out_21
  // Probe on out_8
  // Probe on out_22
  // Probe on out_9
  // Probe on out_23
  // Probe on out_10
  // Probe on out_24
  // Probe on out_11
  // Probe on out_25
  // Probe on out_12
  // Probe on out_26
  // Probe on out_13
  // Probe on out_27
  // Probe on out_14
  // Probe on out_28

  // Other names for the same wires on the sheet: R0[31:0] = out_1; R1[31:0] = out_2; R2[31:0] = out_3;
  //   R3[31:0] = out_4; R4[31:0] = out_5; R5[31:0] = out_6; R6[31:0] = out_7; R7[31:0] = out_8; R8[31:0] = out_9;
  //   R9[31:0] = out_10; R10[31:0] = out_11; R11[31:0] = out_12; R12[31:0] = out_13; R13[31:0] = out_14;
  //   R14[31:0] = out_15; R15[31:0] = out_16; R16[31:0] = out_17; R17[31:0] = out_18; R18[31:0] = out_19;
  //   R19[31:0] = out_20; R20[31:0] = out_21; R21[31:0] = out_22; R22[31:0] = out_23; R23[31:0] = out_24;
  //   R24[31:0] = out_25; R25[31:0] = out_26; R26[31:0] = out_27; R27[31:0] = out_28; R28[31:0] = out_29;
  //   R29[31:0] = out_30; R30[31:0] = out_31; R31[31:0] = out_32
endmodule
